# Fritzing sketch broadcast_schematic (saved by Fritzing 1.0.4)
breadboards: 1

parts:
  M1 = ESP-01 Adapter [part_number=ESP8266]
  부품1 = Arduino Uno (Rev3)
  AHT1 = AHT20 BMP280 pressure and humidity breakout

nets:
  N1: M1.RX, 부품1.D3_PWM
  N2: M1.TX, 부품1.D2
  VCC: M1.VCC, 부품1.3V3, AHT1.VDD
  GND: M1.GND, 부품1.GND, AHT1.GND
  N3: 부품1.A4/SDA, AHT1.SDA
  N4: 부품1.A5/SCL, AHT1.SCL

custom parts:
  ESP-01 Adapter: Generic ESP-10 Adapter module with ESP8266 wireless module installed.
  AHT20 BMP280 pressure and humidity breakout: Cheap breakout board for the BMP280, barometric pressure sensor, and AHT20, humidity sensor
